# Fritzing sketch breadboard (saved by Fritzing 0.9.3b)
breadboards: 1

parts:
  パーツ1 = Arduino Uno (Rev3)
  R1 = Resistor [tolerance=±5% resistance=10k package=THT]
  R2 = PHOTOCELL [package=photocell]

nets:
  N1: パーツ1.A0, R1.Pin_0, R2.P$1
  N2: パーツ1.5V, R2.P$2
  N3: パーツ1.GND, R1.Pin_1
