# Fritzing sketch circuit (saved by Fritzing 0.9.3b)
breadboards: 1

parts:
  パーツ1 = Arduino Uno (Rev3)
  part = DC Power [voltage=5 frequency=60]
  CdS = PHOTOCELL [package=photocell-kit]
  part_2 = DC Power [voltage=5 frequency=60]
  part_3 = Resistor [tolerance=±5% resistance=10k package=THT]

nets:
  N1: パーツ1.A0, CdS.P$2, part_3.Pin_1
  GND: パーツ1.GND, part_3.Pin_0
  N2: パーツ1.5V, part.V+
  N3: CdS.P$1, part_2.V-
