# Fritzing sketch breadboard (saved by Fritzing 0.9.3b)
breadboards: 1

parts:
  パーツ1 = Arduino Uno (Rev3)
  Q1 = NPN-Transistor [package="TO92 [THT]"]
  D1 = Diode [package=diode-1n4001]
  M1 = DC Motor
  VCC1 = Battery

nets:
  N1: パーツ1.D11_PWM/MOSI, Q1.C
  N2: パーツ1.GND, Q1.E, M1.pin_1, VCC1.-
  N3: Q1.B, D1.A, M1.pin_2
  N4: D1.C, VCC1.+
