# Fritzing sketch breadboard (saved by Fritzing 0.9.3b)
breadboards: 1

parts:
  パーツ1 = Arduino Uno (Rev3)
  R1 = Resistor [tolerance=±5% resistance=150 package=THT]
  LED2 = RGB LED (com. cathode, rgb) [package="5 mm [THT]"]
  R2 = Resistor [tolerance=±5% resistance=150 package=THT]
  R3 = Resistor [tolerance=±5% resistance=150 package=THT]

nets:
  N1: パーツ1.GND, LED2.common_cathode
  N2: パーツ1.D3_PWM, R1.Pin_1
  N3: パーツ1.D5_PWM, R2.Pin_1
  N4: パーツ1.D6_PWM, R3.Pin_1
  N5: R1.Pin_0, LED2.blue_anode
  N6: LED2.red_anode, R3.Pin_0
  N7: LED2.green_anode, R2.Pin_0
