# Fritzing sketch breadboard (saved by Fritzing 0.9.3b)
breadboards: 1

parts:
  パーツ1 = Arduino Uno (Rev3)
  IC1 = IC, DIP package, 8 pins [chip_label=KXR94-2050]

nets:
  N1: パーツ1.A0, IC1.pin6
  N2: パーツ1.A1, IC1.pin7
  N3: パーツ1.A2, IC1.pin8
  N4: パーツ1.5V, IC1.pin1, IC1.pin2
  N5: パーツ1.GND, IC1.pin3
  N6: IC1.pin4, IC1.pin5
