# Fritzing sketch breadboard (saved by Fritzing 0.9.3b)

parts:
  パーツ1 = Arduino Uno (Rev3)
  Grove1 = Grove OLED 128x96

nets:
  GND: パーツ1.GND, Grove1.GND
  N1: パーツ1.A4/SDA, Grove1.SDA
  N2: パーツ1.A5/SCL, Grove1.SCL
  3V3: パーツ1.3V3, Grove1.VCC

notes:
  SCL
  SDA
