# Fritzing sketch circuit (saved by Fritzing 0.9.3b)
breadboards: 1

parts:
  パーツ1 = Arduino Uno (Rev3)
  part = DC Power [voltage=3.3V frequency=60]
  AQM0802A = Grove OLED 128x96
  V2 = DC Power [voltage=3.3V frequency=60]

nets:
  N1: パーツ1.A4/SDA, AQM0802A.SCL
  N2: パーツ1.A5/SCL, AQM0802A.SDA
  GND: パーツ1.GND, AQM0802A.GND
  N3: パーツ1.3V3, part.V+
  N4: AQM0802A.VCC, V2.V-

notes:
  SDA
  SCL
