# Fritzing sketch circuit (saved by Fritzing 0.9.3b)
breadboards: 1

parts:
  パーツ1 = Arduino Uno (Rev3)
  part = LED - 5mm [color="Red (633nm)" package="5 mm [THT]"]
  part_2 = Resistor [tolerance=±5% resistance=100 package=THT]

nets:
  N1: パーツ1.D13/SCK, part_2.Pin_0
  GND: パーツ1.GND, part.cathode
  N2: part.anode, part_2.Pin_1
