# Fritzing sketch breadboard (saved by Fritzing 0.9.3b)
breadboards: 1

parts:
  パーツ1 = Arduino Uno (Rev3)
  U1 = 74HC595 SMD [package="SO16 [SMD]"]
  R3 = Resistor [tolerance=±5% resistance=1k package=THT]
  R4 = Resistor [tolerance=±5% resistance=1k package=THT]
  LED1 = LED - 3mm [color="Red (633nm)" package="3 mm [THT]"]
  R5 = Resistor [tolerance=±5% resistance=1k package=THT]
  R6 = Resistor [tolerance=±5% resistance=1k package=THT]
  R7 = Resistor [tolerance=±5% resistance=1k package=THT]
  R8 = Resistor [tolerance=±5% resistance=1k package=THT]
  R9 = Resistor [tolerance=±5% resistance=1k package=THT]
  R10 = Resistor [tolerance=±5% resistance=1k package=THT]
  LED2 = LED - 3mm [color="Red (633nm)" package="3 mm [THT]"]
  LED3 = LED - 3mm [color="Red (633nm)" package="3 mm [THT]"]
  LED4 = LED - 3mm [color="Red (633nm)" package="3 mm [THT]"]
  LED5 = LED - 3mm [color="Red (633nm)" package="3 mm [THT]"]
  LED6 = LED - 3mm [color="Red (633nm)" package="3 mm [THT]"]
  LED7 = LED - 3mm [color="Red (633nm)" package="3 mm [THT]"]
  LED8 = LED - 3mm [color="Red (633nm)" package="3 mm [THT]"]

nets:
  N1: パーツ1.D5_PWM, U1.SH_CP
  N2: パーツ1.D6_PWM, U1.ST_CP
  N3: パーツ1.D7, U1.DS
  5V: パーツ1.5V, U1.MR, U1.VCC
  GND: パーツ1.GND, U1.GND, U1.OE, R3.Pin_1, R4.Pin_1, R5.Pin_1, R6.Pin_1, R7.Pin_1, R8.Pin_1, R9.Pin_1, R10.Pin_1
  N4: U1.Q1, LED2.anode
  N5: U1.Q2, LED3.anode
  N6: U1.Q3, LED4.anode
  N7: U1.Q4, LED5.anode
  N8: U1.Q5, LED6.anode
  N9: U1.Q6, LED7.anode
  N10: U1.Q7, LED8.anode
  N11: U1.Q0, LED1.anode
  N12: R3.Pin_0, LED1.cathode
  N13: R4.Pin_0, LED2.cathode
  N14: R5.Pin_0, LED3.cathode
  N15: R6.Pin_0, LED4.cathode
  N16: R7.Pin_0, LED5.cathode
  N17: R8.Pin_0, LED6.cathode
  N18: R9.Pin_0, LED7.cathode
  N19: R10.Pin_0, LED8.cathode
