# Fritzing sketch circuit (saved by Fritzing 0.9.3b)
breadboards: 1

parts:
  パーツ1 = Arduino Uno (Rev3)
  SPEAKER = Piezo Speaker

nets:
  N1: パーツ1.D13/SCK, SPEAKER.pin1
  GND: パーツ1.GND, SPEAKER.pin2
