# Fritzing sketch breadboard (saved by Fritzing 0.9.3b)
breadboards: 1

parts:
  パーツ1 = Arduino Uno (Rev3)
  LED1 = smd LED [color="Red (633nm)" package="0805 [SMD]"]
  R1 = Resistor [tolerance=±5% resistance=100 package=THT]
  S1 = Pushbutton [package="[THT]"]
  R2 = Resistor [tolerance=±5% resistance=10k package=THT]

nets:
  N1: パーツ1.D9_PWM, S1.Pin_3, S1.Pin_4, R2.Pin_1
  N2: パーツ1.D13/SCK, R1.Pin_1
  N3: パーツ1.GND, LED1.cathode, R2.Pin_0
  N4: パーツ1.5V, S1.Pin_1, S1.Pin_2
  N5: LED1.anode, R1.Pin_0
