# Fritzing sketch circuit (saved by Fritzing 0.9.3b)
breadboards: 1

parts:
  パーツ1 = Arduino Uno (Rev3)
  LED1 = LED - 5mm [color="Red (633nm)" package="5 mm [THT]"]
  R1 = Resistor [tolerance=±5% resistance=100 package=THT]
  TACT_Switch = Pushbutton [package="[THT]"]
  V1 = DC Power [voltage=5 frequency=60]
  V2 = DC Power [voltage=5 frequency=60]
  R2 = Resistor [tolerance=±5% resistance=10k package=THT]

nets:
  N1: パーツ1.D13/SCK, R1.Pin_0
  GND: パーツ1.GND, LED1.cathode, R2.Pin_0
  N2: パーツ1.D6_PWM, TACT_Switch.Pin_3, TACT_Switch.Pin_4, V2.V+, R2.Pin_1
  N3: パーツ1.5V, V1.V+
  N4: LED1.anode, R1.Pin_1
