# Fritzing sketch circuit (saved by Fritzing 0.9.3b)
breadboards: 1

parts:
  パーツ1 = Arduino Uno (Rev3)
  V1 = DC Power [voltage=5 frequency=60]
  part = DC Power [voltage=5 frequency=60]
  LM35 = LM35 Temperature Sensor [package="TO92 [THT]"]

nets:
  N1: パーツ1.A0, LM35.Vout
  GND: パーツ1.GND, LM35.GND
  N2: パーツ1.5V, V1.V+
  N3: part.V-, LM35.+Vs
