# Fritzing sketch breadboard (saved by Fritzing 0.9.3b)
breadboards: 1

parts:
  パーツ1 = Arduino Uno (Rev3)
  HC-SR04_Sensor_1 = HC-SR04 Ultrasonic Distance Sensor

nets:
  N1: パーツ1.D8, HC-SR04_Sensor_1.ECHO
  N2: パーツ1.D13/SCK, HC-SR04_Sensor_1.TRIG
  5V: パーツ1.5V, HC-SR04_Sensor_1.VCC
  GND: パーツ1.GND, HC-SR04_Sensor_1.GND
