# Fritzing sketch circuit (saved by Fritzing 0.9.3b)
breadboards: 1

parts:
  パーツ1 = Arduino Uno (Rev3)
  HC-SR04 = HC-SR04 Ultrasonic Distance Sensor
  V2 = DC Power [voltage=5 frequency=60]
  part = DC Power [voltage=5 frequency=60]

nets:
  N1: パーツ1.D8, HC-SR04.GND
  N2: パーツ1.D13/SCK, HC-SR04.TRIG
  GND: パーツ1.GND, HC-SR04.ECHO
  N3: パーツ1.5V, V2.V+
  N4: HC-SR04.VCC, part.V-
