# Fritzing sketch breadboard (saved by Fritzing 0.9.3b)
breadboards: 1

parts:
  パーツ1 = Arduino Uno (Rev3)
  R1 = Trimmer Potentiometer [maximum_resistance=10kΩ package=THT]

nets:
  N1: パーツ1.A0, R1.wiper
  N2: パーツ1.5V, R1.leg2
  N3: パーツ1.GND, R1.leg1
