# Fritzing sketch circuit (saved by Fritzing 0.9.3b)
breadboards: 1

parts:
  パーツ1 = Arduino Uno (Rev3)
  V1 = DC Power [voltage=5 frequency=60]
  Volume(10Ω~5MΩ) = Trimmer Potentiometer [maximum_resistance=10kΩ package=THT]
  V2 = DC Power [voltage=5 frequency=60]

nets:
  N1: パーツ1.A0, Volume(10Ω~5MΩ).wiper
  GND: パーツ1.GND, Volume(10Ω~5MΩ).leg1
  N2: パーツ1.5V, V1.V+
  N3: Volume(10Ω~5MΩ).leg2, V2.V-
